// Logisim project LIUSHUIXIAN.circ as structural Verilog: 22 circuits, main circuit main
module main (
  input  in_1,
  output [31:0] Instr,
  output RegWrite,
  output [4:0] RegAddr,
  output [31:0] RegData,
  output MemWrite,
  output [4:0] MemAddr,
  output [31:0] MemData
);

  wire alu_1_out_4, ALUSrc, Branch_beq, Branch_j, Branch_jal, Branch_jr, CLK, d_e_1_alusrc_o, e_m_1_out_22,
       e_m_1_out_23, em_memwrite, em_regwrite, flush_e, fu_1_frtmsel, MemRead, memWrite_t, regWrite_t,
       STALLD, STALLF, zero;
  wire [1:0] Bsel, d_e_1_memtoreg_o, d_e_1_regdst_o, e_m_1_out_25, EXTOP, fu_1_frsdsel, fu_1_frsesel,
       fu_1_frtdsel, fu_1_frtesel, m_w_1_out_28, memToReg, RegDst, ssel, tuse1_d, tuse2_d;
  wire [2:0] npcop;
  wire [3:0] ALUOP, aluop_t, tnew_e, tnew_m, tnew_w;
  wire [4:0] _15_11, _20_16, _25_21, d_e_1_rd_o, d_e_1_rs_o, d_e_1_rt_o, des_e, des_m, des_w, e_m_1_out_17,
       s1_d, s1_e, s2_d, s2_e, s2_m, writereg_e;
  wire [5:0] FUNCT, OP;
  wire [9:0] pc_1_out_6;
  wire [15:0] _15_0;
  wire [25:0] _25_0;
  wire [31:0] adder_1_out, adder_2_out, addr, alu_w, aluresult, bit_extender_1_out, d_cmp_rs, d_cmp_rt,
       d_e_1_out_36, e_alu_a, e_alu_b, e_m_1_out_16, e_m_1_pc_4_o, e_m_1_pc_o, em_pc, em_pc_4, em_pc_8, EtoD,
       extendresult, instr_em, instr_m, m_dm_wd, m_w_1_out_20, MemAddr_t, MtoD, multiplexer_6_out, npc,
       pc_1_out_5, PC_4_O, pc_8_m, PC_8_O, pc_8_w, PC_O, rd1, rd2, rom_1_data, rs_e, rt_e, str, writedata_mw,
       WtoD;

  Clock clock_1 (.out(CLK));
  assign bit_extender_1_out = {{14{_15_0[15]}}, {_15_0, 2'b00}};  // Bit_Extender bit_extender_1
  EXTEND extend_1 (.in_1(_15_0), .in_2(EXTOP), .out_3(extendresult));
  PC pc_1 (.NPC(npc), .in_2(STALLF), .out_5(pc_1_out_5), .out_6(pc_1_out_6), .in_3(CLK), .in_4(in_1));
  // Probe on pc_1_out_6
  npc npc_1 (
    .pc(pc_1_out_5), .str(str), .extend(bit_extender_1_out), .zero(zero), .rs(d_cmp_rs), .in_6(npcop),
    .out_7(npc));
  // Probe on pc_1_out_5
  ROM #(.addrWidth(10), .dataWidth(32)) rom_1 (.addr(pc_1_out_6), .data(rom_1_data));  // open: sel
  Adder #(.width(32)) adder_1 (.a(pc_1_out_5), .b(32'h4), .out(adder_1_out));  // open: cin, cout
  Adder #(.width(32)) adder_2 (.a(pc_1_out_5), .b(32'h8), .out(adder_2_out));  // open: cin, cout
  F_D f_d_1 (
    .instr_i(rom_1_data), .pc_i(pc_1_out_5), .instr_o(str), .in_1(CLK), .in_2(in_1), .in_7(STALLD),
    .pc_o(PC_O), .pc_4_o(PC_4_O), .pc_8_o(PC_8_O), .pc_4_i(adder_1_out), .pc_8_i(adder_2_out));
  D d_1 (.in_1(str), .out_2(s1_d), .out_3(s2_d), .tuse1_d(tuse1_d), .tuse2_d(tuse2_d));
  E e_1 (
    .in_1(instr_em), .in_2(d_e_1_out_36), .in_3(em_pc_8), .out_4(s1_e), .out_5(s2_e), .out_6(tnew_e),
    .out_7(des_e), .out_8(EtoD));
  M m_1 (
    .in_1(instr_m), .alu(addr), .pc_8(pc_8_m), .out_5(s2_m), .out_7(des_m), .out_8(MtoD), .alu_2(addr));  // open: out_6
  W w_1 (
    .in_1(Instr), .regdata(RegData), .alu(alu_w), .ext(alu_w), .pc_8(pc_8_w), .out_7(des_w), .out_8(WtoD));  // open: out_6
  STALL stall_1 (
    .s1_D(s1_d), .s2_D(s2_d), .tUse1_D(tuse1_d), .tUse2_D(tuse2_d), .des_E(des_e), .tNew_E(tnew_e),
    .tNew_M(tnew_m), .des_M(des_m), .Stall_F(STALLF), .Stall_D(STALLD), .flush_E(flush_e));
  Multiplexer #(.select(2), .width(32), .enable("false")) multiplexer_1 (
    .in0(rd1), .in1(EtoD), .in2(MtoD), .in3({32{1'b0}}), .out(d_cmp_rs), .sel(fu_1_frsdsel));
  SPLITTER splitter_1 (
    .in_1(str), .OP(OP), .FUNCT(FUNCT), ._0_25(_25_0), ._0_15(_15_0), ._21_25(_25_21), ._16_20(_20_16),
    ._11_15(_15_11));
  Multiplexer #(.select(2), .width(32), .enable("false")) multiplexer_2 (
    .in0(rd2), .in1(EtoD), .in2(MtoD), .in3({32{1'b0}}), .out(d_cmp_rt), .sel(fu_1_frtdsel));
  CONTRILLER contriller_1 (
    .OP(OP), .FUNCT(FUNCT), .RegDst(RegDst), .RegWrite(regWrite_t), .ALUSrc(ALUSrc), .Branch_beq(Branch_beq),
    .MemRead(MemRead), .MemWrite(memWrite_t), .Extop(EXTOP), .MemtoReg(memToReg), .ALUOP(ALUOP),
    .Branch_jal(Branch_jal), .Branch_j(Branch_j), .Branch_jR(Branch_jr), .out_19(Bsel), .out_21(ssel));  // open: s1, s2, T1, T2, TN
  GRF grf_1 (
    .A1(_25_21), .A2(_20_16), .A3(RegAddr), .WD(RegData), .clk(CLK), .reset(in_1), .we(RegWrite), .RD1(rd1),
    .RD2(rd2));
  Comparator #(.width(32)) comparator_1 (.a(d_cmp_rs), .b(d_cmp_rt), .eq(zero));  // open: gt, lt
  Multiplexer #(.select(2), .width(32), .enable("false")) multiplexer_3 (
    .in0(rs_e), .in1(MtoD), .in2(WtoD), .in3({32{1'b0}}), .out(e_alu_a), .sel(fu_1_frsesel));
  D_E d_e_1 (
    .pc_i(PC_O), .RD1_i(d_cmp_rs), .pc_4_i(PC_4_O), .RD2_i(d_cmp_rt), .pc_8_i(PC_8_O), .rs_i(_25_21),
    .rt_i(_20_16), .rd_i(_15_11), .instr_i(str), .pc_o(em_pc), .RD1_o(rs_e), .pc_4_o(em_pc_4), .RD2_o(rt_e),
    .pc_8_o(em_pc_8), .rs_o(d_e_1_rs_o), .rt_o(d_e_1_rt_o), .rd_o(d_e_1_rd_o), .out_33(instr_em), .in_1(CLK),
    .in_2(in_1), .in_20(flush_e), .regdst_o(d_e_1_regdst_o), .regdst_i(RegDst), .memwrite_i(memWrite_t),
    .memwrite_o(em_memwrite), .regwrite_i(regWrite_t), .regwrite_o(em_regwrite), .alusrc_i(ALUSrc),
    .alusrc_o(d_e_1_alusrc_o), .memread_i(MemRead), .memtoreg_i(memToReg), .memtoreg_o(d_e_1_memtoreg_o),
    .aluop_i(ALUOP), .aluop_o(aluop_t), .out_36(d_e_1_out_36), .extsult_i(extendresult));  // open: memread_o
  FU fu_1 (
    .s1_D(s1_d), .s2_D(s2_d), .s1_E(s1_e), .s2_E(s2_e), .des_E(des_e), .tNew_E(tnew_e), .s2_M(s2_m),
    .tNew_M(tnew_m), .des_M(des_m), .tNew_W(tnew_w), .des_W(des_w), .fRsDsel(fu_1_frsdsel),
    .fRtDsel(fu_1_frtdsel), .fRsEsel(fu_1_frsesel), .fRtEsel(fu_1_frtesel), .fRtMsel(fu_1_frtmsel));
  Multiplexer #(.select(2), .width(32), .enable("false")) multiplexer_4 (
    .in0(rt_e), .in1(MtoD), .in2(WtoD), .in3({32{1'b0}}), .out(e_alu_b), .sel(fu_1_frtesel));
  Multiplexer #(.select(2), .width(5), .enable("false")) multiplexer_5 (
    .in0(d_e_1_rt_o), .in1(d_e_1_rd_o), .in2({5{1'b1}}), .out(writereg_e), .sel(d_e_1_regdst_o));  // open: in3
  npcop npcop_1 (.beq(Branch_beq), .jr(Branch_jr), .bne(1'b0), .out_6(npcop), .jal_2(Branch_jal), .jal(Branch_j));
  Multiplexer #(.width(32), .enable("false")) multiplexer_6 (
    .in0(e_alu_b), .in1(d_e_1_out_36), .out(multiplexer_6_out), .sel(d_e_1_alusrc_o));
  Multiplexer #(.width(32), .enable("false")) multiplexer_7 (
    .in0(e_m_1_out_16), .in1(WtoD), .out(m_dm_wd), .sel(fu_1_frtmsel));
  ALU alu_1 (.ALUOP(aluop_t), .A(e_alu_a), .B(multiplexer_6_out), .out_4(alu_1_out_4), .out_5(aluresult));
  E_M e_m_1 (
    .aluresult_i(aluresult), .writedata_i(e_alu_b), .writereg_i(writereg_e), .pc_i(em_pc), .pc_4_i(em_pc_4),
    .pc_8_i(em_pc_8), .instr_i(instr_em), .out_15(addr), .out_16(e_m_1_out_16), .out_17(e_m_1_out_17),
    .pc_o(e_m_1_pc_o), .pc_4_o(e_m_1_pc_4_o), .pc_8_o(pc_8_m), .out_21(instr_m), .in_1(CLK), .in_2(in_1),
    .memwrite_i(em_memwrite), .out_22(e_m_1_out_22), .out_23(e_m_1_out_23), .memtoreg_i(d_e_1_memtoreg_o),
    .out_25(e_m_1_out_25), .regwrite_i(em_regwrite), .in_14(tnew_e), .out_26(tnew_m));  // open: memread_i, out_24
  DM dm_1 (
    .A(addr), .in_3(m_dm_wd), .SSEL(Bsel), .BSEL(ssel), .RD(writedata_mw), .DMWR(e_m_1_out_22), .CLK(CLK),
    .RESET(in_1));
  M_W m_w_1 (
    .writereg_i(e_m_1_out_17), .aluresult_i(addr), .writedata_i(e_m_1_out_16), .readdata_i(writedata_mw),
    .pc_i(e_m_1_pc_o), .pc_4_i(e_m_1_pc_4_o), .pc_8_i(pc_8_m), .instr_i(instr_m), .memaddr(addr),
    .memdata(m_dm_wd), .memwrite(e_m_1_out_22), .out_17(RegAddr), .out_18(alu_w), .out_20(m_w_1_out_20),
    .pc_8_o(pc_8_w), .out_24(Instr), .out_25({MemAddr_t[31:7], MemAddr, MemAddr_t[1:0]}), .out_26(MemData),
    .out_27(MemWrite), .in_1(CLK), .in_2(in_1), .out_30(tnew_w), .in_16(tnew_m), .regwrite(e_m_1_out_23),
    .out_29(RegWrite), .memtoreg(e_m_1_out_25), .out_28(m_w_1_out_28));  // open: out_19, pc_o, pc_4_o
  Multiplexer #(.select(2), .width(32), .enable("false")) multiplexer_8 (
    .in0(alu_w), .in1(m_w_1_out_20), .in2(pc_8_w), .out(RegData), .sel(m_w_1_out_28));  // open: in3

  // Other names for the same wires on the sheet: instr_w[31:0] = Instr; MemAddr_t[6:2] = MemAddr; Reset = in_1
endmodule

module GRF (
  input  [4:0] A1,
  input  clk,
  input  reset,
  input  we,
  input  [4:0] A2,
  input  [4:0] A3,
  input  [31:0] WD,
  output [31:0] RD1,
  output [31:0] RD2
);

  wire and_1_out, and_2_out, comparator_1_eq, comparator_2_eq, comparator_3_eq, comparator_4_eq;
  wire [31:0] I0, I1, I2, I3, I4, I5, I6, I7, I8, I9, I10, I11, I12, I13, I14, I15, I16, I17, I18, I19, I20,
       I21, I22, I23, I24, I25, I26, I27, I28, I29, I30, I31, multiplexer_2_out, multiplexer_4_out, O0, O1,
       O2, O3, O4, O5, O6, O7, O8, O9, O10, O11, O12, O13, O14, O15, O16, O17, O18, O19, O20, O21, O22, O23,
       O24, O25, O26, O27, O28, O29, O30, O31, RD1_t, RD2_t;

  Demultiplexer #(.select(5), .width(32), .tristate("true")) demultiplexer_1 (
    .out0(I0), .out1(I1), .out2(I2), .out3(I3), .out4(I4), .out5(I5), .out6(I6), .out7(I7), .out8(I8),
    .out9(I9), .out10(I10), .out11(I11), .out12(I12), .out13(I13), .out14(I14), .out15(I15), .out16(I16),
    .out17(I17), .out18(I18), .out19(I19), .out20(I20), .out21(I21), .out22(I22), .out23(I23), .out24(I24),
    .out25(I25), .out26(I26), .out27(I27), .out28(I28), .out29(I29), .out30(I30), .out31(I31), .in(WD),
    .sel(A3));  // open: en
  Multiplexer #(.select(5), .width(32)) multiplexer_1 (
    .in0(O0), .in1(O1), .in2(O2), .in3(O3), .in4(O4), .in5(O5), .in6(O6), .in7(O7), .in8(O8), .in9(O9),
    .in10(O10), .in11(O11), .in12(O12), .in13(O13), .in14(O14), .in15(O15), .in16(O16), .in17(O17),
    .in18(O18), .in19(O19), .in20(O20), .in21(O21), .in22(O22), .in23(O23), .in24(O24), .in25(O25),
    .in26(O26), .in27(O27), .in28(O28), .in29(O29), .in30(O30), .in31(O31), .out(RD2_t), .sel(A2));  // open: en
  Comparator #(.width(5), .mode("unsigned")) comparator_1 (.a(A1), .b(A3), .eq(comparator_1_eq));  // open: gt, lt
  and and_1 (and_1_out, comparator_1_eq, we);
  Comparator #(.width(5), .mode("unsigned")) comparator_2 (.a(A2), .b(A3), .eq(comparator_2_eq));  // open: gt, lt
  Comparator #(.width(5), .mode("unsigned")) comparator_3 (
    .a(A1), .b({5{1'b0}}), .eq(comparator_3_eq));  // open: gt, lt
  Comparator #(.width(5), .mode("unsigned")) comparator_4 (
    .a(A2), .b({5{1'b0}}), .eq(comparator_4_eq));  // open: gt, lt
  and and_2 (and_2_out, comparator_2_eq, we);
  Multiplexer #(.width(32), .enable("false")) multiplexer_2 (
    .in0(RD1_t), .in1(WD), .out(multiplexer_2_out), .sel(and_1_out));
  Multiplexer #(.select(5), .width(32)) multiplexer_3 (
    .in0(O0), .in1(O1), .in2(O2), .in3(O3), .in4(O4), .in5(O5), .in6(O6), .in7(O7), .in8(O8), .in9(O9),
    .in10(O10), .in11(O11), .in12(O12), .in13(O13), .in14(O14), .in15(O15), .in16(O16), .in17(O17),
    .in18(O18), .in19(O19), .in20(O20), .in21(O21), .in22(O22), .in23(O23), .in24(O24), .in25(O25),
    .in26(O26), .in27(O27), .in28(O28), .in29(O29), .in30(O30), .in31(O31), .out(RD1_t), .sel(A1));  // open: en
  Multiplexer #(.width(32), .enable("false")) multiplexer_4 (
    .in0(RD2_t), .in1(WD), .out(multiplexer_4_out), .sel(and_2_out));
  Multiplexer #(.width(32), .enable("false")) multiplexer_5 (
    .in0(multiplexer_2_out), .in1({32{1'b0}}), .out(RD1), .sel(comparator_3_eq));
  Multiplexer #(.width(32), .enable("false")) multiplexer_6 (
    .in0(multiplexer_4_out), .in1({32{1'b0}}), .out(RD2), .sel(comparator_4_eq));
  Register #(.width(32)) register_1 (.D({32{1'b0}}), .en(we), .Q(O0), .clk(clk), .clr(reset));
  Register #(.width(32)) register_2 (.D(I8), .en(we), .Q(O8), .clk(clk), .clr(reset));
  Register #(.width(32)) register_3 (.D(I16), .en(we), .Q(O16), .clk(clk), .clr(reset));
  Register #(.width(32)) register_4 (.D(I24), .en(we), .Q(O24), .clk(clk), .clr(reset));
  Register #(.width(32)) register_5 (.D(I1), .en(we), .Q(O1), .clk(clk), .clr(reset));
  Register #(.width(32)) register_6 (.D(I9), .en(we), .Q(O9), .clk(clk), .clr(reset));
  Register #(.width(32)) register_7 (.D(I17), .en(we), .Q(O17), .clk(clk), .clr(reset));
  Register #(.width(32)) register_8 (.D(I25), .en(we), .Q(O25), .clk(clk), .clr(reset));
  Register #(.width(32)) register_9 (.D(I2), .en(we), .Q(O2), .clk(clk), .clr(reset));
  Register #(.width(32)) register_10 (.D(I10), .en(we), .Q(O10), .clk(clk), .clr(reset));
  Register #(.width(32)) register_11 (.D(I18), .en(we), .Q(O18), .clk(clk), .clr(reset));
  Register #(.width(32)) register_12 (.D(I26), .en(we), .Q(O26), .clk(clk), .clr(reset));
  Register #(.width(32)) register_13 (.D(I3), .en(we), .Q(O3), .clk(clk), .clr(reset));
  Register #(.width(32)) register_14 (.D(I11), .en(we), .Q(O11), .clk(clk), .clr(reset));
  Register #(.width(32)) register_15 (.D(I19), .en(we), .Q(O19), .clk(clk), .clr(reset));
  Register #(.width(32)) register_16 (.D(I27), .en(we), .Q(O27), .clk(clk), .clr(reset));
  Register #(.width(32)) register_17 (.D(I4), .en(we), .Q(O4), .clk(clk), .clr(reset));
  Register #(.width(32)) register_18 (.D(I12), .en(we), .Q(O12), .clk(clk), .clr(reset));
  Register #(.width(32)) register_19 (.D(I20), .en(we), .Q(O20), .clk(clk), .clr(reset));
  Register #(.width(32)) register_20 (.D(I28), .en(we), .Q(O28), .clk(clk), .clr(reset));
  Register #(.width(32)) register_21 (.D(I5), .en(we), .Q(O5), .clk(clk), .clr(reset));
  Register #(.width(32)) register_22 (.D(I13), .en(we), .Q(O13), .clk(clk), .clr(reset));
  Register #(.width(32)) register_23 (.D(I21), .en(we), .Q(O21), .clk(clk), .clr(reset));
  Register #(.width(32)) register_24 (.D(I29), .en(we), .Q(O29), .clk(clk), .clr(reset));
  Register #(.width(32)) register_25 (.D(I6), .en(we), .Q(O6), .clk(clk), .clr(reset));
  Register #(.width(32)) register_26 (.D(I14), .en(we), .Q(O14), .clk(clk), .clr(reset));
  Register #(.width(32)) register_27 (.D(I22), .en(we), .Q(O22), .clk(clk), .clr(reset));
  Register #(.width(32)) register_28 (.D(I30), .en(we), .Q(O30), .clk(clk), .clr(reset));
  Register #(.width(32)) register_29 (.D(I7), .en(we), .Q(O7), .clk(clk), .clr(reset));
  Register #(.width(32)) register_30 (.D(I15), .en(we), .Q(O15), .clk(clk), .clr(reset));
  Register #(.width(32)) register_31 (.D(I23), .en(we), .Q(O23), .clk(clk), .clr(reset));
  Register #(.width(32)) register_32 (.D(I31), .en(we), .Q(O31), .clk(clk), .clr(reset));
endmodule

module CONTRILLER (
  input  [5:0] OP,
  input  [5:0] FUNCT,
  output [1:0] RegDst,
  output RegWrite,
  output ALUSrc,
  output Branch_beq,
  output Branch_jal,
  output Branch_j,
  output Branch_jR,
  output MemRead,
  output MemWrite,
  output [1:0] Extop,
  output [1:0] MemtoReg,
  output [3:0] ALUOP,
  output [1:0] T1,
  output [1:0] T2,
  output [3:0] TN,
  output s1,
  output [1:0] out_19,
  output s2,
  output [1:0] out_21
);

  wire ADDU, BNE, LB, LH, multiplexer_1_out, NOP, not_1_out, not_2_out, not_3_out, not_4_out, not_5_out,
       not_6_out, not_7_out, not_8_out, not_9_out, not_10_out, not_11_out, not_12_out, or_4_out, or_5_out,
       or_6_out, or_7_out, or_8_out, or_10_out, R, SB, SH, SUBU;

  not not_1 (not_1_out, OP[5]);
  not not_2 (not_2_out, OP[4]);
  not not_3 (not_3_out, OP[3]);
  or or_1 (RegDst[0], ADDU, SUBU);
  not not_4 (not_4_out, OP[2]);
  not not_5 (not_5_out, OP[1]);
  not not_6 (not_6_out, OP[0]);
  and LW (MemRead, OP[5], not_2_out, not_3_out, not_4_out, OP[1], OP[0]);
  and SW (MemWrite, OP[5], not_2_out, OP[3], not_4_out, OP[1], OP[0]);
  and u_R (R, not_1_out, not_2_out, not_3_out, not_4_out, not_5_out, not_6_out);
  and ORI (ALUOP[2], not_1_out, not_2_out, OP[3], OP[2], not_5_out, OP[0]);
  and J (Branch_j, not_1_out, not_2_out, not_3_out, not_4_out, OP[1], not_6_out);
  and BEQ (Branch_beq, not_1_out, not_2_out, not_3_out, OP[2], not_5_out, not_6_out);
  and JAL (Branch_jal, not_1_out, not_2_out, not_3_out, not_4_out, OP[1], OP[0]);
  and LUI (Extop[1], not_1_out, not_2_out, OP[3], OP[2], OP[1], OP[0]);
  and ADDIU (Extop[0], not_1_out, not_2_out, OP[3], not_4_out, not_5_out, OP[0]);
  and u_BNE (BNE, not_1_out, not_2_out, not_3_out, OP[2], not_5_out, OP[0]);
  and u_LB (LB, OP[5], not_2_out, not_3_out, not_4_out, not_5_out, not_6_out);
  and u_LH (LH, OP[5], not_2_out, not_3_out, not_4_out, not_5_out, OP[0]);
  and u_SB (SB, OP[5], not_2_out, OP[3], not_4_out, not_5_out, not_6_out);
  and u_SH (SH, OP[5], not_2_out, OP[3], not_4_out, not_5_out, OP[0]);
  or or_2 (s2, MemWrite, RegDst[0], Branch_beq);
  not not_7 (not_7_out, FUNCT[5]);
  or or_3 (s1, MemRead, MemWrite, RegDst[0], ALUOP[2]);
  not not_8 (not_8_out, FUNCT[4]);
  not not_9 (not_9_out, FUNCT[3]);
  not not_10 (not_10_out, FUNCT[2]);
  not not_11 (not_11_out, FUNCT[1]);
  not not_12 (not_12_out, FUNCT[0]);
  sblb sblb_1 (.SB(SB), .SH(SH), .out_5(out_19));  // open: LB, LH
  sblb sblb_2 (.SB(LB), .SH(LH), .out_5(out_21));  // open: LB, LH
  and u_ADDU (ADDU, R, FUNCT[5], not_8_out, not_9_out, not_10_out, not_11_out, FUNCT[0]);
  and u_SUBU (SUBU, R, FUNCT[5], not_8_out, not_9_out, not_10_out, FUNCT[1], FUNCT[0]);
  and u_NOP (NOP, R, not_7_out, not_8_out, not_9_out, not_10_out, not_11_out, not_12_out);
  and JR (Branch_jR, R, not_7_out, not_8_out, FUNCT[3], not_10_out, not_11_out, not_12_out);
  or or_4 (or_4_out, MemRead, MemWrite, RegDst[0], ALUOP[2]);
  buf or_5 (or_5_out, RegDst[0]);  // OR_Gate
  or or_6 (or_6_out, Extop[1], Branch_jal);
  or or_7 (or_7_out, RegDst[0], ALUOP[2]);
  or or_8 (or_8_out, MemRead, Branch_jal);
  or or_9 (ALUOP[1], Branch_beq, SUBU);
  Priority_Encoder #(.select(2)) priority_encoder_1 (
    .in0(Branch_beq), .in1(or_4_out), .out(T1));  // open: in2, in3, gs, en_out, en_in
  Priority_Encoder #(.select(2)) priority_encoder_2 (
    .in0(Branch_beq), .in1(or_5_out), .in2(MemWrite), .out(T2));  // open: in3, gs, en_out, en_in
  Priority_Encoder #(.select(4)) priority_encoder_3 (
    .in0(or_6_out), .in1(or_7_out), .in2(MemRead), .out(TN));  // open: in3, in4, in5, in6, in7, in8, in9, in10, in11, in12, in13, in14, in15, gs, en_out, en_in
  or or_10 (or_10_out, RegDst[0], MemRead, Branch_jal, Extop[1], ALUOP[2]);
  or or_11 (ALUOP[0], MemRead, MemWrite, Extop[1], ADDU);
  Multiplexer #(.enable("false")) multiplexer_1 (.in0(1'b1), .in1(1'b0), .out(multiplexer_1_out), .sel(or_8_out));
  Multiplexer #(.enable("false")) multiplexer_2 (.in0(or_10_out), .in1(1'b0), .out(RegWrite), .sel(NOP));
  Priority_Encoder #(.select(2)) priority_encoder_4 (
    .in0(multiplexer_1_out), .in1(MemRead), .in2(Branch_jal), .out(MemtoReg));  // open: in3, gs, en_out, en_in
  or or_12 (ALUSrc, MemRead, MemWrite, Extop[1], ALUOP[2]);

  assign ALUOP[3] = 1'b0;
  assign RegDst[1] = Branch_jal;

  // Other names for the same wires on the sheet: tunnel = ALUOP[0]; tunnel_t = ALUOP[1]; _1 = ALUOP[2];
  //   cal_i = ALUOP[2]; ORI = ALUOP[2]; b_type = Branch_beq; BEQ = Branch_beq; ADDIU = Extop[0]; LUI = Extop[1];
  //   J = Branch_j; JR = Branch_jR; LW = MemRead; cal_r = RegDst[0]; JAL = Branch_jal; SW = MemWrite
endmodule

// 0-25
module SPLITTER (
  input  [31:0] in_1,
  output [5:0] OP,
  output [5:0] FUNCT,
  output [25:0] _0_25,
  output [15:0] _0_15,
  output [4:0] _21_25,
  output [4:0] _16_20,
  output [4:0] _11_15
);


  assign _0_15 = in_1[15:0];
  assign _0_25 = in_1[25:0];
  assign _11_15 = in_1[15:11];
  assign _16_20 = in_1[20:16];
  assign _21_25 = in_1[25:21];
  assign FUNCT = in_1[5:0];
  assign OP = in_1[31:26];
endmodule

module PC (
  input  [31:0] NPC,
  input  in_2,
  input  in_3,
  input  in_4,
  output [31:0] out_5,
  output [9:0] out_6
);

  wire comparator_1_eq, not_1_out;
  wire [31:0] register_1_q, subtractor_1_out;

  not not_1 (not_1_out, in_2);
  Register #(.width(32)) register_1 (.D(NPC), .en(not_1_out), .Q(register_1_q), .clk(in_3), .clr(in_4));
  Comparator #(.width(32), .mode("unsigned")) comparator_1 (
    .a(register_1_q), .b({32{1'b0}}), .eq(comparator_1_eq));  // open: gt, lt
  Multiplexer #(.width(32), .enable("false")) multiplexer_1 (
    .in0(register_1_q), .in1(32'h3000), .out(out_5), .sel(comparator_1_eq));
  Subtractor #(.width(32)) subtractor_1 (
    .a(out_5), .b(32'h3000), .out({subtractor_1_out[31:12], out_6, subtractor_1_out[1:0]}));  // open: bin, bout
endmodule

module D_E (
  input  in_1,
  input  in_2,
  input  [31:0] pc_i,
  input  [31:0] RD1_i,
  input  [31:0] pc_4_i,
  input  [31:0] RD2_i,
  input  [31:0] pc_8_i,
  input  [4:0] rs_i,
  input  [1:0] regdst_i,
  input  [4:0] rt_i,
  input  memwrite_i,
  input  [4:0] rd_i,
  input  regwrite_i,
  input  alusrc_i,
  input  [31:0] instr_i,
  input  memread_i,
  input  [1:0] memtoreg_i,
  input  [3:0] aluop_i,
  input  [31:0] extsult_i,
  input  in_20,
  output [31:0] pc_o,
  output [31:0] RD1_o,
  output [31:0] pc_4_o,
  output [31:0] RD2_o,
  output [31:0] pc_8_o,
  output [4:0] rs_o,
  output [1:0] regdst_o,
  output [4:0] rt_o,
  output memwrite_o,
  output [4:0] rd_o,
  output regwrite_o,
  output alusrc_o,
  output [31:0] out_33,
  output memread_o,
  output [1:0] memtoreg_o,
  output [31:0] out_36,
  output [3:0] aluop_o
);

  wire multiplexer_12_out, multiplexer_13_out, multiplexer_14_out, multiplexer_15_out;
  wire [1:0] multiplexer_11_out, multiplexer_16_out;
  wire [3:0] multiplexer_17_out;
  wire [4:0] multiplexer_3_out, multiplexer_4_out, multiplexer_5_out;
  wire [31:0] multiplexer_1_out, multiplexer_2_out, multiplexer_6_out, multiplexer_7_out, multiplexer_8_out,
       multiplexer_9_out, multiplexer_10_out;

  Multiplexer #(.width(32), .enable("false")) multiplexer_1 (
    .in0(RD1_i), .in1({32{1'b0}}), .out(multiplexer_1_out), .sel(in_20));
  Multiplexer #(.width(32), .enable("false")) multiplexer_2 (
    .in0(RD2_i), .in1({32{1'b0}}), .out(multiplexer_2_out), .sel(in_20));
  Multiplexer #(.width(5), .enable("false")) multiplexer_3 (
    .in0(rs_i), .in1({5{1'b0}}), .out(multiplexer_3_out), .sel(in_20));
  Multiplexer #(.width(5), .enable("false")) multiplexer_4 (
    .in0(rt_i), .in1({5{1'b0}}), .out(multiplexer_4_out), .sel(in_20));
  Multiplexer #(.width(5), .enable("false")) multiplexer_5 (
    .in0(rd_i), .in1({5{1'b0}}), .out(multiplexer_5_out), .sel(in_20));
  Multiplexer #(.width(32), .enable("false")) multiplexer_6 (
    .in0(instr_i), .in1({32{1'b0}}), .out(multiplexer_6_out), .sel(in_20));
  Multiplexer #(.width(32), .enable("false")) multiplexer_7 (
    .in0(extsult_i), .in1({32{1'b0}}), .out(multiplexer_7_out), .sel(in_20));
  Register #(.width(32)) register_1 (.D(multiplexer_1_out), .Q(RD1_o), .clk(in_1), .clr(in_2));  // open: en
  Register #(.width(32)) register_2 (.D(multiplexer_2_out), .Q(RD2_o), .clk(in_1), .clr(in_2));  // open: en
  Register #(.width(5)) register_3 (.D(multiplexer_3_out), .Q(rs_o), .clk(in_1), .clr(in_2));  // open: en
  Register #(.width(5)) register_4 (.D(multiplexer_4_out), .Q(rt_o), .clk(in_1), .clr(in_2));  // open: en
  Register #(.width(5)) register_5 (.D(multiplexer_5_out), .Q(rd_o), .clk(in_1), .clr(in_2));  // open: en
  Register #(.width(32)) register_6 (.D(multiplexer_6_out), .Q(out_33), .clk(in_1), .clr(in_2));  // open: en
  Register #(.width(32)) register_7 (.D(multiplexer_7_out), .Q(out_36), .clk(in_1), .clr(in_2));  // open: en
  Multiplexer #(.width(32), .enable("false")) multiplexer_8 (
    .in0(pc_i), .in1({32{1'b0}}), .out(multiplexer_8_out), .sel(in_20));
  Multiplexer #(.width(32), .enable("false")) multiplexer_9 (
    .in0(pc_4_i), .in1({32{1'b0}}), .out(multiplexer_9_out), .sel(in_20));
  Multiplexer #(.width(32), .enable("false")) multiplexer_10 (
    .in0(pc_8_i), .in1({32{1'b0}}), .out(multiplexer_10_out), .sel(in_20));
  Multiplexer #(.width(2), .enable("false")) multiplexer_11 (
    .in0(regdst_i), .in1(2'b00), .out(multiplexer_11_out), .sel(in_20));
  Multiplexer #(.enable("false")) multiplexer_12 (.in0(memwrite_i), .in1(1'b0), .out(multiplexer_12_out), .sel(in_20));
  Multiplexer #(.enable("false")) multiplexer_13 (.in0(regwrite_i), .in1(1'b0), .out(multiplexer_13_out), .sel(in_20));
  Multiplexer #(.enable("false")) multiplexer_14 (.in0(alusrc_i), .in1(1'b0), .out(multiplexer_14_out), .sel(in_20));
  Multiplexer #(.enable("false")) multiplexer_15 (.in0(memread_i), .in1(1'b0), .out(multiplexer_15_out), .sel(in_20));
  Multiplexer #(.width(2), .enable("false")) multiplexer_16 (
    .in0(memtoreg_i), .in1(2'b00), .out(multiplexer_16_out), .sel(in_20));
  Multiplexer #(.width(4), .enable("false")) multiplexer_17 (
    .in0(aluop_i), .in1(4'b0000), .out(multiplexer_17_out), .sel(in_20));
  Register #(.width(32)) register_8 (.D(multiplexer_8_out), .Q(pc_o), .clk(in_1), .clr(in_2));  // open: en
  Register #(.width(4)) register_9 (.D(multiplexer_17_out), .Q(aluop_o), .clk(in_1), .clr(in_2));  // open: en
  Register #(.width(32)) register_10 (.D(multiplexer_9_out), .Q(pc_4_o), .clk(in_1), .clr(in_2));  // open: en
  Register #(.width(32)) register_11 (.D(multiplexer_10_out), .Q(pc_8_o), .clk(in_1), .clr(in_2));  // open: en
  Register #(.width(2)) register_12 (.D(multiplexer_11_out), .Q(regdst_o), .clk(in_1), .clr(in_2));  // open: en
  Register #(.width(1)) register_13 (.D(multiplexer_12_out), .Q(memwrite_o), .clk(in_1), .clr(in_2));  // open: en
  Register #(.width(1)) register_14 (.D(multiplexer_13_out), .Q(regwrite_o), .clk(in_1), .clr(in_2));  // open: en
  Register #(.width(1)) register_15 (.D(multiplexer_14_out), .Q(alusrc_o), .clk(in_1), .clr(in_2));  // open: en
  Register #(.width(1)) register_16 (.D(multiplexer_15_out), .Q(memread_o), .clk(in_1), .clr(in_2));  // open: en
  Register #(.width(2)) register_17 (.D(multiplexer_16_out), .Q(memtoreg_o), .clk(in_1), .clr(in_2));  // open: en

  // Other names for the same wires on the sheet: clk = in_1; clk_prime = in_1; flush = in_20; Reset = in_2
endmodule

module E_M (
  input  in_1,
  input  in_2,
  input  [31:0] aluresult_i,
  input  [31:0] writedata_i,
  input  [4:0] writereg_i,
  input  [31:0] pc_i,
  input  [31:0] pc_4_i,
  input  [31:0] pc_8_i,
  input  [31:0] instr_i,
  input  memwrite_i,
  input  regwrite_i,
  input  memread_i,
  input  [1:0] memtoreg_i,
  input  [3:0] in_14,
  output [31:0] out_15,
  output [31:0] out_16,
  output [4:0] out_17,
  output [31:0] pc_o,
  output [31:0] pc_4_o,
  output [31:0] pc_8_o,
  output [31:0] out_21,
  output out_22,
  output out_23,
  output out_24,
  output [1:0] out_25,
  output [3:0] out_26
);

  wire comparator_1_lt;
  wire [3:0] multiplexer_1_out, subtractor_1_out;

  Subtractor #(.width(4)) subtractor_1 (.a(in_14), .b(4'b0001), .out(subtractor_1_out));  // open: bin, bout
  Register #(.width(32)) register_1 (.D(aluresult_i), .Q(out_15), .clk(in_1), .clr(in_2));  // open: en
  Register #(.width(32)) register_2 (.D(writedata_i), .Q(out_16), .clk(in_1), .clr(in_2));  // open: en
  Register #(.width(5)) register_3 (.D(writereg_i), .Q(out_17), .clk(in_1), .clr(in_2));  // open: en
  Register #(.width(32)) register_4 (.D(pc_i), .Q(pc_o), .clk(in_1), .clr(in_2));  // open: en
  Register #(.width(32)) register_5 (.D(pc_4_i), .Q(pc_4_o), .clk(in_1), .clr(in_2));  // open: en
  Register #(.width(32)) register_6 (.D(pc_8_i), .Q(pc_8_o), .clk(in_1), .clr(in_2));  // open: en
  Register #(.width(32)) register_7 (.D(instr_i), .Q(out_21), .clk(in_1), .clr(in_2));  // open: en
  Register #(.width(1)) register_8 (.D(memwrite_i), .Q(out_22), .clk(in_1), .clr(in_2));  // open: en
  Register #(.width(1)) register_9 (.D(regwrite_i), .Q(out_23), .clk(in_1), .clr(in_2));  // open: en
  Register #(.width(1)) register_10 (.D(memread_i), .Q(out_24), .clk(in_1), .clr(in_2));  // open: en
  Register #(.width(2)) register_11 (.D(memtoreg_i), .Q(out_25), .clk(in_1), .clr(in_2));  // open: en
  Comparator #(.width(4)) comparator_1 (.a(subtractor_1_out), .b(4'b0000), .lt(comparator_1_lt));  // open: gt, eq
  Multiplexer #(.width(4), .enable("false")) multiplexer_1 (
    .in0(subtractor_1_out), .in1(4'b0000), .out(multiplexer_1_out), .sel(comparator_1_lt));
  Register #(.width(4)) register_12 (.D(multiplexer_1_out), .Q(out_26), .clk(in_1), .clr(in_2));  // open: en

  // Other names for the same wires on the sheet: clk = in_1; clk_prime = in_1; Reset = in_2
endmodule

module F_D (
  input  in_1,
  input  in_2,
  input  [31:0] instr_i,
  input  [31:0] pc_i,
  input  [31:0] pc_4_i,
  input  [31:0] pc_8_i,
  input  in_7,
  output [31:0] instr_o,
  output [31:0] pc_o,
  output [31:0] pc_4_o,
  output [31:0] pc_8_o
);

  wire clk_prime, not_1_out, not_2_out, not_3_out, not_4_out;

  not not_1 (not_1_out, in_7);
  not not_2 (not_2_out, in_7);
  not not_3 (not_3_out, in_7);
  buf and_1 (clk_prime, in_1);  // AND_Gate
  Register #(.width(32)) register_1 (.D(instr_i), .en(not_1_out), .Q(instr_o), .clk(clk_prime), .clr(in_2));
  Register #(.width(32)) register_2 (.D(pc_i), .en(not_2_out), .Q(pc_o), .clk(clk_prime), .clr(in_2));
  Register #(.width(32)) register_3 (.D(pc_4_i), .en(not_3_out), .Q(pc_4_o), .clk(clk_prime), .clr(in_2));
  not not_4 (not_4_out, in_7);
  Register #(.width(32)) register_4 (.D(pc_8_i), .en(not_4_out), .Q(pc_8_o), .clk(clk_prime), .clr(in_2));

  // Other names for the same wires on the sheet: clk = in_1; F_D_stall = in_7; reset = in_2
endmodule

module M_W (
  input  in_1,
  input  in_2,
  input  [4:0] writereg_i,
  input  [31:0] aluresult_i,
  input  [31:0] writedata_i,
  input  [31:0] readdata_i,
  input  [31:0] pc_i,
  input  [31:0] pc_4_i,
  input  [31:0] pc_8_i,
  input  [31:0] instr_i,
  input  [31:0] memaddr,
  input  [31:0] memdata,
  input  memwrite,
  input  [1:0] memtoreg,
  input  regwrite,
  input  [3:0] in_16,
  output [4:0] out_17,
  output [31:0] out_18,
  output [31:0] out_19,
  output [31:0] out_20,
  output [31:0] pc_o,
  output [31:0] pc_4_o,
  output [31:0] pc_8_o,
  output [31:0] out_24,
  output [31:0] out_25,
  output [31:0] out_26,
  output out_27,
  output [1:0] out_28,
  output out_29,
  output [3:0] out_30
);

  wire comparator_1_lt;
  wire [3:0] multiplexer_1_out, subtractor_1_out;

  Subtractor #(.width(4)) subtractor_1 (.a(in_16), .b(4'b0001), .out(subtractor_1_out));  // open: bin, bout
  Register #(.width(5)) register_1 (.D(writereg_i), .Q(out_17), .clk(in_1), .clr(in_2));  // open: en
  Register #(.width(32)) register_2 (.D(aluresult_i), .Q(out_18), .clk(in_1), .clr(in_2));  // open: en
  Register #(.width(32)) register_3 (.D(writedata_i), .Q(out_19), .clk(in_1), .clr(in_2));  // open: en
  Register #(.width(32)) register_4 (.D(readdata_i), .Q(out_20), .clk(in_1), .clr(in_2));  // open: en
  Register #(.width(32)) register_5 (.D(pc_i), .Q(pc_o), .clk(in_1), .clr(in_2));  // open: en
  Register #(.width(32)) register_6 (.D(pc_4_i), .Q(pc_4_o), .clk(in_1), .clr(in_2));  // open: en
  Register #(.width(32)) register_7 (.D(pc_8_i), .Q(pc_8_o), .clk(in_1), .clr(in_2));  // open: en
  Register #(.width(32)) register_8 (.D(instr_i), .Q(out_24), .clk(in_1), .clr(in_2));  // open: en
  Register #(.width(32)) register_9 (.D(memaddr), .Q(out_25), .clk(in_1), .clr(in_2));  // open: en
  Register #(.width(32)) register_10 (.D(memdata), .Q(out_26), .clk(in_1), .clr(in_2));  // open: en
  Register #(.width(1)) register_11 (.D(memwrite), .Q(out_27), .clk(in_1), .clr(in_2));  // open: en
  Register #(.width(2)) register_12 (.D(memtoreg), .Q(out_28), .clk(in_1), .clr(in_2));  // open: en
  Register #(.width(1)) register_13 (.D(regwrite), .Q(out_29), .clk(in_1), .clr(in_2));  // open: en
  Comparator #(.width(4)) comparator_1 (.a(subtractor_1_out), .b(4'b0000), .lt(comparator_1_lt));  // open: gt, eq
  Multiplexer #(.width(4), .enable("false")) multiplexer_1 (
    .in0(subtractor_1_out), .in1(4'b0000), .out(multiplexer_1_out), .sel(comparator_1_lt));
  Register #(.width(4)) register_14 (.D(multiplexer_1_out), .Q(out_30), .clk(in_1), .clr(in_2));  // open: en

  // Other names for the same wires on the sheet: clk = in_1; clk_prime = in_1; Reset = in_2
endmodule

module FU (
  input  [4:0] s1_D,
  input  [4:0] s2_D,
  input  [4:0] s1_E,
  input  [4:0] s2_E,
  input  [4:0] des_E,
  input  [3:0] tNew_E,
  input  [4:0] s2_M,
  input  [3:0] tNew_M,
  input  [4:0] des_M,
  input  [3:0] tNew_W,
  input  [4:0] des_W,
  output [1:0] fRsDsel,
  output [1:0] fRtDsel,
  output [1:0] fRsEsel,
  output [1:0] fRtEsel,
  output fRtMsel
);

  wire and_1_out, and_2_out, and_3_out, and_4_out, and_5_out, and_6_out, and_7_out, and_8_out, and_9_out,
       comparator_1_eq, comparator_2_eq, comparator_3_eq, comparator_4_eq, comparator_5_eq, comparator_6_eq,
       comparator_7_eq, comparator_8_eq, comparator_9_eq, comparator_10_eq, comparator_11_eq,
       comparator_12_eq, comparator_13_eq, comparator_14_eq, comparator_15_eq, comparator_16_eq,
       comparator_17_eq, comparator_18_eq, comparator_19_eq, comparator_20_eq, comparator_21_eq,
       comparator_22_eq, comparator_23_eq, comparator_24_eq, comparator_25_eq, comparator_26_eq,
       comparator_27_eq, not_1_out, not_2_out, not_3_out, not_4_out, not_5_out, not_6_out, not_7_out,
       not_8_out, not_9_out, undriven;
  wire [1:0] multiplexer_1_out, multiplexer_2_out, multiplexer_5_out, multiplexer_6_out;

  // Probe on undriven
  Comparator #(.width(5), .mode("unsigned")) comparator_1 (
    .a(s1_D), .b({5{1'b0}}), .eq(comparator_1_eq));  // open: gt, lt
  not not_1 (not_1_out, comparator_1_eq);
  Comparator #(.width(5), .mode("unsigned")) comparator_2 (.a(s1_D), .b(des_M), .eq(comparator_2_eq));  // open: gt, lt
  Comparator #(.width(4), .mode("unsigned")) comparator_3 (
    .a(tNew_M), .b(4'b0000), .eq(comparator_3_eq));  // open: gt, lt
  not not_2 (not_2_out, comparator_4_eq);
  Comparator #(.width(5), .mode("unsigned")) comparator_4 (
    .a(s1_D), .b({5{1'b0}}), .eq(comparator_4_eq));  // open: gt, lt
  Comparator #(.width(5), .mode("unsigned")) comparator_5 (.a(s1_D), .b(des_E), .eq(comparator_5_eq));  // open: gt, lt
  Comparator #(.width(4), .mode("unsigned")) comparator_6 (
    .a(tNew_E), .b(4'b0000), .eq(comparator_6_eq));  // open: gt, lt
  Comparator #(.width(5), .mode("unsigned")) comparator_7 (
    .a(s2_D), .b({5{1'b0}}), .eq(comparator_7_eq));  // open: gt, lt
  Comparator #(.width(5), .mode("unsigned")) comparator_8 (.a(s2_D), .b(des_M), .eq(comparator_8_eq));  // open: gt, lt
  Comparator #(.width(4), .mode("unsigned")) comparator_9 (
    .a(tNew_M), .b(4'b0000), .eq(comparator_9_eq));  // open: gt, lt
  Comparator #(.width(5), .mode("unsigned")) comparator_10 (
    .a(s2_D), .b({5{1'b0}}), .eq(comparator_10_eq));  // open: gt, lt
  Comparator #(.width(5), .mode("unsigned")) comparator_11 (
    .a(s2_D), .b(des_E), .eq(comparator_11_eq));  // open: gt, lt
  Comparator #(.width(4), .mode("unsigned")) comparator_12 (
    .a(tNew_E), .b(4'b0000), .eq(comparator_12_eq));  // open: gt, lt
  and and_1 (and_1_out, not_1_out, comparator_2_eq, comparator_3_eq);
  and and_2 (and_2_out, not_2_out, comparator_5_eq, comparator_6_eq);
  not not_3 (not_3_out, comparator_7_eq);
  not not_4 (not_4_out, comparator_10_eq);
  Multiplexer #(.width(2)) multiplexer_1 (
    .in0(2'b00), .in1(2'b10), .out(multiplexer_1_out), .sel(and_1_out));  // open: en
  and and_3 (and_3_out, not_3_out, comparator_8_eq, comparator_9_eq);
  and and_4 (and_4_out, not_4_out, comparator_11_eq, comparator_12_eq);
  Multiplexer #(.width(2)) multiplexer_2 (
    .in0(2'b00), .in1(2'b10), .out(multiplexer_2_out), .sel(and_3_out));  // open: en
  Multiplexer #(.width(2)) multiplexer_3 (
    .in0(multiplexer_1_out), .in1(2'b01), .out(fRsDsel), .sel(and_2_out));  // open: en
  Multiplexer #(.width(2)) multiplexer_4 (
    .in0(multiplexer_2_out), .in1(2'b01), .out(fRtDsel), .sel(and_4_out));  // open: en
  Comparator #(.width(5), .mode("unsigned")) comparator_13 (
    .a(s1_E), .b({5{1'b0}}), .eq(comparator_13_eq));  // open: gt, lt
  Comparator #(.width(5), .mode("unsigned")) comparator_14 (
    .a(s1_E), .b(des_W), .eq(comparator_14_eq));  // open: gt, lt
  Comparator #(.width(4), .mode("unsigned")) comparator_15 (
    .a(tNew_W), .b(4'b0000), .eq(comparator_15_eq));  // open: gt, lt
  Comparator #(.width(5), .mode("unsigned")) comparator_16 (
    .a(s1_E), .b({5{1'b0}}), .eq(comparator_16_eq));  // open: gt, lt
  Comparator #(.width(5), .mode("unsigned")) comparator_17 (
    .a(s1_E), .b(des_M), .eq(comparator_17_eq));  // open: gt, lt
  Comparator #(.width(4), .mode("unsigned")) comparator_18 (
    .a(tNew_M), .b(4'b0000), .eq(comparator_18_eq));  // open: gt, lt
  Comparator #(.width(5), .mode("unsigned")) comparator_19 (
    .a(s2_E), .b({5{1'b0}}), .eq(comparator_19_eq));  // open: gt, lt
  Comparator #(.width(5), .mode("unsigned")) comparator_20 (
    .a(s2_E), .b(des_W), .eq(comparator_20_eq));  // open: gt, lt
  Comparator #(.width(4), .mode("unsigned")) comparator_21 (
    .a(tNew_W), .b(4'b0000), .eq(comparator_21_eq));  // open: gt, lt
  Comparator #(.width(5), .mode("unsigned")) comparator_22 (
    .a(s2_E), .b({5{1'b0}}), .eq(comparator_22_eq));  // open: gt, lt
  Comparator #(.width(5), .mode("unsigned")) comparator_23 (
    .a(s2_E), .b(des_M), .eq(comparator_23_eq));  // open: gt, lt
  Comparator #(.width(4), .mode("unsigned")) comparator_24 (
    .a(tNew_M), .b(4'b0000), .eq(comparator_24_eq));  // open: gt, lt
  not not_5 (not_5_out, comparator_13_eq);
  not not_6 (not_6_out, comparator_16_eq);
  not not_7 (not_7_out, comparator_19_eq);
  not not_8 (not_8_out, comparator_22_eq);
  and and_5 (and_5_out, not_5_out, comparator_14_eq, comparator_15_eq);
  and and_6 (and_6_out, not_6_out, comparator_17_eq, comparator_18_eq);
  and and_7 (and_7_out, not_7_out, comparator_20_eq, comparator_21_eq);
  and and_8 (and_8_out, not_8_out, comparator_23_eq, comparator_24_eq);
  Multiplexer #(.width(2)) multiplexer_5 (
    .in0(2'b00), .in1(2'b10), .out(multiplexer_5_out), .sel(and_5_out));  // open: en
  Multiplexer #(.width(2)) multiplexer_6 (
    .in0(2'b00), .in1(2'b10), .out(multiplexer_6_out), .sel(and_7_out));  // open: en
  Multiplexer #(.width(2)) multiplexer_7 (
    .in0(multiplexer_5_out), .in1(2'b01), .out(fRsEsel), .sel(and_6_out));  // open: en
  Multiplexer #(.width(2)) multiplexer_8 (
    .in0(multiplexer_6_out), .in1(2'b01), .out(fRtEsel), .sel(and_8_out));  // open: en
  Comparator #(.width(5), .mode("unsigned")) comparator_25 (
    .a(s2_M), .b({5{1'b0}}), .eq(comparator_25_eq));  // open: gt, lt
  not not_9 (not_9_out, comparator_25_eq);
  Comparator #(.width(5), .mode("unsigned")) comparator_26 (
    .a(s2_M), .b(des_W), .eq(comparator_26_eq));  // open: gt, lt
  Comparator #(.width(4), .mode("unsigned")) comparator_27 (
    .a(tNew_W), .b(4'b0000), .eq(comparator_27_eq));  // open: gt, lt
  and and_9 (and_9_out, not_9_out, comparator_26_eq, comparator_27_eq);
  Multiplexer multiplexer_9 (.in0(1'b0), .in1(1'b1), .out(fRtMsel), .sel(and_9_out));  // open: en
endmodule

module STALL (
  input  [4:0] s1_D,
  input  [4:0] s2_D,
  input  [1:0] tUse1_D,
  input  [1:0] tUse2_D,
  input  [4:0] des_E,
  input  [3:0] tNew_E,
  input  [3:0] tNew_M,
  input  [4:0] des_M,
  output Stall_F,
  output Stall_D,
  output flush_E
);

  wire and_1_out, and_2_out, and_3_out, and_4_out, comparator_1_eq, comparator_2_eq, comparator_3_lt,
       comparator_4_eq, comparator_5_eq, comparator_6_lt, comparator_7_eq, comparator_8_eq, comparator_9_lt,
       comparator_10_eq, comparator_11_eq, comparator_12_lt, not_1_out, not_2_out, not_3_out, not_4_out;
  wire [3:0] tUse1_D_t, tUse2_D_t;

  Comparator #(.width(5), .mode("unsigned")) comparator_1 (
    .a(s1_D), .b({5{1'b0}}), .eq(comparator_1_eq));  // open: gt, lt
  Comparator #(.width(5), .mode("unsigned")) comparator_2 (.a(s1_D), .b(des_E), .eq(comparator_2_eq));  // open: gt, lt
  Comparator #(.width(4), .mode("unsigned")) comparator_3 (
    .a(tUse1_D_t), .b(tNew_E), .lt(comparator_3_lt));  // open: gt, eq
  Comparator #(.width(5), .mode("unsigned")) comparator_4 (
    .a(s2_D), .b({5{1'b0}}), .eq(comparator_4_eq));  // open: gt, lt
  Comparator #(.width(5), .mode("unsigned")) comparator_5 (.a(s2_D), .b(des_E), .eq(comparator_5_eq));  // open: gt, lt
  Comparator #(.width(4), .mode("unsigned")) comparator_6 (
    .a(tUse2_D_t), .b(tNew_E), .lt(comparator_6_lt));  // open: gt, eq
  Comparator #(.width(5), .mode("unsigned")) comparator_7 (
    .a(s1_D), .b({5{1'b0}}), .eq(comparator_7_eq));  // open: gt, lt
  Comparator #(.width(5), .mode("unsigned")) comparator_8 (.a(s1_D), .b(des_M), .eq(comparator_8_eq));  // open: gt, lt
  Comparator #(.width(4), .mode("unsigned")) comparator_9 (
    .a(tUse1_D_t), .b(tNew_M), .lt(comparator_9_lt));  // open: gt, eq
  Comparator #(.width(5), .mode("unsigned")) comparator_10 (
    .a(s2_D), .b({5{1'b0}}), .eq(comparator_10_eq));  // open: gt, lt
  Comparator #(.width(5), .mode("unsigned")) comparator_11 (
    .a(s2_D), .b(des_M), .eq(comparator_11_eq));  // open: gt, lt
  Comparator #(.width(4), .mode("unsigned")) comparator_12 (
    .a(tUse2_D_t), .b(tNew_M), .lt(comparator_12_lt));  // open: gt, eq
  assign tUse1_D_t = {{2{1'b0}}, tUse1_D};  // Bit_Extender bit_extender_1
  not not_1 (not_1_out, comparator_1_eq);
  not not_2 (not_2_out, comparator_4_eq);
  not not_3 (not_3_out, comparator_7_eq);
  not not_4 (not_4_out, comparator_10_eq);
  and and_1 (and_1_out, not_1_out, comparator_2_eq, comparator_3_lt);
  and and_2 (and_2_out, not_2_out, comparator_5_eq, comparator_6_lt);
  and and_3 (and_3_out, not_3_out, comparator_8_eq, comparator_9_lt);
  and and_4 (and_4_out, not_4_out, comparator_11_eq, comparator_12_lt);
  assign tUse2_D_t = {{2{1'b0}}, tUse2_D};  // Bit_Extender bit_extender_2
  or or_1 (flush_E, and_1_out, and_2_out, and_3_out, and_4_out);

  assign Stall_D = flush_E;
  assign Stall_F = flush_E;

  // Other names for the same wires on the sheet: stall_flag = flush_E
endmodule

module ALU (
  input  [3:0] ALUOP,
  input  [31:0] A,
  input  [31:0] B,
  output out_4,
  output [31:0] out_5
);

  wire [31:0] adder_1_out, or_1_out, subtractor_1_out;

  Adder #(.width(32)) adder_1 (.a(A), .b(B), .out(adder_1_out));  // open: cin, cout
  Subtractor #(.width(32)) subtractor_1 (.a(A), .b(B), .out(subtractor_1_out));  // open: bin, bout
  assign or_1_out = A | B;  // OR_Gate or_1, 32 bits wide
  // Probe on ALUOP
  Multiplexer #(.select(4), .width(32), .enable("false")) multiplexer_1 (
    .in1(adder_1_out), .in2(subtractor_1_out), .in4(or_1_out), .out(out_5), .sel(ALUOP));  // open: in0, in3, in5, in6, in7, in8, in9, in10, in11, in12, in13, in14, in15
  Comparator #(.width(32)) comparator_1 (.a(subtractor_1_out), .b({32{1'b0}}), .eq(out_4));  // open: gt, lt
endmodule

module DM (
  input  [31:0] A,
  input  [1:0] SSEL,
  input  [31:0] in_3,
  input  [1:0] BSEL,
  input  DMWR,
  input  CLK,
  input  RESET,
  output [31:0] RD
);

  wire decoder_1_out0, decoder_1_out1, decoder_1_out2, decoder_1_out3, decoder_2_out0, decoder_2_out1;
  wire [7:0] _0_7, _8_15, _16_23, _24_31, multiplexer_1_out, multiplexer_2_out, multiplexer_3_out,
       multiplexer_4_out, multiplexer_8_out;
  wire [15:0] multiplexer_5_out, multiplexer_6_out, multiplexer_9_out;
  wire [31:0] bit_extender_1_out, bit_extender_2_out, multiplexer_7_out;

  Decoder #(.select(2)) decoder_1 (
    .out0(decoder_1_out0), .out1(decoder_1_out1), .out2(decoder_1_out2), .out3(decoder_1_out3), .sel(A[1:0]));  // open: en
  Decoder decoder_2 (.out0(decoder_2_out0), .out1(decoder_2_out1), .sel(A[1]));  // open: en
  Multiplexer #(.width(8), .enable("false")) multiplexer_1 (
    .in0(_0_7), .in1(in_3[7:0]), .out(multiplexer_1_out), .sel(decoder_1_out0));
  Multiplexer #(.width(8), .enable("false")) multiplexer_2 (
    .in0(_8_15), .in1(in_3[7:0]), .out(multiplexer_2_out), .sel(decoder_1_out1));
  Multiplexer #(.width(8), .enable("false")) multiplexer_3 (
    .in0(_16_23), .in1(in_3[7:0]), .out(multiplexer_3_out), .sel(decoder_1_out2));
  Multiplexer #(.width(8), .enable("false")) multiplexer_4 (
    .in0(_24_31), .in1(in_3[7:0]), .out(multiplexer_4_out), .sel(decoder_1_out3));
  Multiplexer #(.width(16), .enable("false")) multiplexer_5 (
    .in0({_8_15, _0_7}), .in1(in_3[15:0]), .out(multiplexer_5_out), .sel(decoder_2_out0));
  Multiplexer #(.width(16), .enable("false")) multiplexer_6 (
    .in0({_24_31, _16_23}), .in1(in_3[15:0]), .out(multiplexer_6_out), .sel(decoder_2_out1));
  // Probe on multiplexer_7_out
  Multiplexer #(.select(2), .width(32), .enable("false")) multiplexer_7 (
    .in0(in_3), .in1({multiplexer_4_out, multiplexer_3_out, multiplexer_2_out, multiplexer_1_out}),
    .in2({multiplexer_6_out, multiplexer_5_out}), .out(multiplexer_7_out), .sel(SSEL));  // open: in3
  RAM #(.addrWidth(5), .dataWidth(32), .bus("separate")) ram_1 (
    .addr(A[6:2]), .din(multiplexer_7_out), .data({_24_31, _16_23, _8_15, _0_7}), .str(DMWR), .clk(CLK),
    .clr(RESET));  // open: sel, ld
  Multiplexer #(.select(2), .width(8), .enable("false")) multiplexer_8 (
    .in0(_0_7), .in1(_8_15), .in2(_16_23), .in3(_24_31), .out(multiplexer_8_out), .sel(A[1:0]));
  Multiplexer #(.width(16), .enable("false")) multiplexer_9 (
    .in0({_8_15, _0_7}), .in1({_24_31, _16_23}), .out(multiplexer_9_out), .sel(A[1]));
  assign bit_extender_1_out = {{24{multiplexer_8_out[7]}}, multiplexer_8_out};  // Bit_Extender bit_extender_1
  assign bit_extender_2_out = {{16{multiplexer_9_out[15]}}, multiplexer_9_out};  // Bit_Extender bit_extender_2
  Multiplexer #(.select(2), .width(32), .enable("false")) multiplexer_10 (
    .in0({_24_31, _16_23, _8_15, _0_7}), .in1(bit_extender_1_out), .in2(bit_extender_2_out), .out(RD),
    .sel(BSEL));  // open: in3
endmodule

module EXTEND (
  input  [15:0] in_1,
  input  [1:0] in_2,
  output [31:0] out_3
);

  wire [31:0] bit_extender_1_out, bit_extender_2_out;

  assign bit_extender_1_out = {{16{1'b0}}, in_1};  // Bit_Extender bit_extender_1
  assign bit_extender_2_out = {{16{in_1[15]}}, in_1};  // Bit_Extender bit_extender_2
  Multiplexer #(.select(2), .width(32), .enable("false")) multiplexer_1 (
    .in0(bit_extender_1_out), .in1(bit_extender_2_out), .in2({in_1, {16{1'b0}}}), .out(out_3), .sel(in_2));  // open: in3
endmodule

module npc (
  input  [31:0] pc,
  input  [31:0] str,
  input  [31:0] extend,
  input  zero,
  input  [31:0] rs,
  input  [2:0] in_6,
  output [31:0] out_7
);

  wire [31:0] beq16, multiplexer_1_out, pc_4;

  Adder #(.width(32)) adder_1 (.a(32'h4), .b(pc), .out(pc_4));  // open: cin, cout
  Adder #(.width(32)) adder_2 (.a(extend), .b(pc), .out(beq16));  // open: cin, cout
  Multiplexer #(.width(32), .enable("false")) multiplexer_1 (
    .in0(pc_4), .in1(beq16), .out(multiplexer_1_out), .sel(zero));
  Multiplexer #(.select(3), .width(32), .enable("false")) multiplexer_2 (
    .in0(pc_4), .in1(multiplexer_1_out), .in2({pc[31:28], str[25:0], 2'b00}), .in3(rs), .out(out_7),
    .sel(in_6));  // open: in4, in5, in6, in7

  // Other names for the same wires on the sheet: j26[31:2] = {pc[31:28], str[25:0]}; jr_rs[31:0] = rs
endmodule

module D (
  input  [31:0] in_1,
  output [4:0] out_2,
  output [4:0] out_3,
  output [1:0] tuse1_d,
  output [1:0] tuse2_d
);

  wire addiu, addu, beq, bne, j, jal, jr, lb, lh, lui, lw, nop, or_1_out, or_2_out, or_3_out, or_4_out,
       or_5_out, or_6_out, or_7_out, or_8_out, or_9_out, or_10_out, or_11_out, ori, sb, sh, subu, sw;
  wire [1:0] bit_extender_1_out;
  wire [4:0] splitter_1__16_20, splitter_1__21_25;
  wire [5:0] splitter_1_funct, splitter_1_op;

  or or_1 (or_1_out, addu, subu, beq, sw);
  SPLITTER splitter_1 (
    .in_1(in_1), .OP(splitter_1_op), .FUNCT(splitter_1_funct), ._21_25(splitter_1__21_25),
    ._16_20(splitter_1__16_20));  // open: _0_25, _0_15, _11_15
  CONTRIL contril_1 (
    .OP(splitter_1_op), .FUNCT(splitter_1_funct), .out_3(lw), .out_4(sw), .out_5(ori), .out_6(j),
    .out_7(beq), .out_8(jal), .out_9(lui), .out_10(addiu), .out_11(bne), .out_12(lb), .out_13(lh),
    .out_14(sb), .out_15(sh), .out_16(addu), .out_17(subu), .out_18(nop), .out_19(jr));
  or or_2 (or_2_out, addu, subu);
  or or_3 (or_3_out, sw, lw);
  buf or_4 (or_4_out, ori);  // OR_Gate
  or or_5 (or_5_out, or_2_out, or_3_out, or_4_out);
  or or_6 (or_6_out, addu, subu);
  assign bit_extender_1_out = {{1{1'b0}}, or_6_out};  // Bit_Extender bit_extender_1
  Multiplexer #(.width(5), .enable("false")) multiplexer_1 (
    .in0({5{1'b0}}), .in1(splitter_1__21_25), .out(out_2), .sel(or_11_out));
  Multiplexer #(.width(5), .enable("false")) multiplexer_2 (
    .in0({5{1'b0}}), .in1(splitter_1__16_20), .out(out_3), .sel(or_1_out));
  Multiplexer #(.width(2), .enable("false")) multiplexer_3 (.in0(2'b00), .in1(2'b01), .out(tuse1_d), .sel(or_5_out));
  Multiplexer #(.width(2), .enable("false")) multiplexer_4 (
    .in0(bit_extender_1_out), .in1(2'b10), .out(tuse2_d), .sel(sw));
  or or_7 (or_7_out, addu, subu);
  or or_8 (or_8_out, sw, lw);
  buf or_9 (or_9_out, ori);  // OR_Gate
  buf or_10 (or_10_out, beq);  // OR_Gate
  or or_11 (or_11_out, or_7_out, or_8_out, or_9_out, or_10_out);
endmodule

module CONTRIL (
  input  [5:0] OP,
  input  [5:0] FUNCT,
  output out_3,
  output out_4,
  output out_5,
  output out_6,
  output out_7,
  output out_8,
  output out_9,
  output out_10,
  output out_11,
  output out_12,
  output out_13,
  output out_14,
  output out_15,
  output out_16,
  output out_17,
  output out_18,
  output out_19
);

  wire not_1_out, not_2_out, not_3_out, not_4_out, not_5_out, not_6_out, not_7_out, not_8_out, not_9_out,
       not_10_out, not_11_out, not_12_out, R;

  not not_1 (not_1_out, OP[5]);
  not not_2 (not_2_out, OP[4]);
  not not_3 (not_3_out, OP[3]);
  not not_4 (not_4_out, OP[2]);
  not not_5 (not_5_out, OP[1]);
  not not_6 (not_6_out, OP[0]);
  and LW (out_3, OP[5], not_2_out, not_3_out, not_4_out, OP[1], OP[0]);
  and SW (out_4, OP[5], not_2_out, OP[3], not_4_out, OP[1], OP[0]);
  and u_R (R, not_1_out, not_2_out, not_3_out, not_4_out, not_5_out, not_6_out);
  and ORI (out_5, not_1_out, not_2_out, OP[3], OP[2], not_5_out, OP[0]);
  and J (out_6, not_1_out, not_2_out, not_3_out, not_4_out, OP[1], not_6_out);
  and BEQ (out_7, not_1_out, not_2_out, not_3_out, OP[2], not_5_out, not_6_out);
  and JAL (out_8, not_1_out, not_2_out, not_3_out, not_4_out, OP[1], OP[0]);
  and LUI (out_9, not_1_out, not_2_out, OP[3], OP[2], OP[1], OP[0]);
  and ADDIU (out_10, not_1_out, not_2_out, OP[3], not_4_out, not_5_out, OP[0]);
  and BNE (out_11, not_1_out, not_2_out, not_3_out, OP[2], not_5_out, OP[0]);
  and LB (out_12, OP[5], not_2_out, not_3_out, not_4_out, not_5_out, not_6_out);
  and LH (out_13, OP[5], not_2_out, not_3_out, not_4_out, not_5_out, OP[0]);
  and SB (out_14, OP[5], not_2_out, OP[3], not_4_out, not_5_out, not_6_out);
  and SH (out_15, OP[5], not_2_out, OP[3], not_4_out, not_5_out, OP[0]);
  not not_7 (not_7_out, FUNCT[5]);
  not not_8 (not_8_out, FUNCT[4]);
  not not_9 (not_9_out, FUNCT[3]);
  not not_10 (not_10_out, FUNCT[2]);
  not not_11 (not_11_out, FUNCT[1]);
  not not_12 (not_12_out, FUNCT[0]);
  and ADDU (out_16, R, FUNCT[5], not_8_out, not_9_out, not_10_out, not_11_out, FUNCT[0]);
  and SUBU (out_17, R, FUNCT[5], not_8_out, not_9_out, not_10_out, FUNCT[1], FUNCT[0]);
  and NOP (out_18, R, not_7_out, not_8_out, not_9_out, not_10_out, not_11_out, not_12_out);
  and JR (out_19, R, not_7_out, not_8_out, FUNCT[3], not_10_out, not_11_out, not_12_out);

  // Other names for the same wires on the sheet: ADDIU = out_10; ADDU = out_16; BEQ = out_7; BNE = out_11; J = out_6;
  //   JAL = out_8; JR = out_19; LB = out_12; LH = out_13; LUI = out_9; LW = out_3; NOP = out_18; ORI = out_5;
  //   SB = out_14; SH = out_15; SUBU = out_17; SW = out_4
endmodule

module E (
  input  [31:0] in_1,
  input  [31:0] in_2,
  input  [31:0] in_3,
  output [4:0] out_4,
  output [4:0] out_5,
  output [3:0] out_6,
  output [4:0] out_7,
  output [31:0] out_8
);

  wire addiu, addu, beq, bne, j, jal, jr, lb, lh, lui, lw, nop, or_1_out, or_2_out, or_3_out, or_4_out,
       or_5_out, or_6_out, or_7_out, or_12_out, or_13_out, or_14_out, or_15_out, ori, sb, sh, subu, sw;
  wire [1:0] multiplexer_1_out, multiplexer_2_out, multiplexer_3_out, multiplexer_4_out, multiplexer_5_out,
       or_8_out, or_10_out, or_11_out;
  wire [4:0] rd, rt, splitter_1__21_25;
  wire [5:0] splitter_1_funct, splitter_1_op;

  or or_1 (or_1_out, addu, subu, sw);
  or or_2 (or_2_out, lw, ori, lui);
  SPLITTER splitter_1 (
    .in_1(in_1), .OP(splitter_1_op), .FUNCT(splitter_1_funct), ._21_25(splitter_1__21_25), ._16_20(rt),
    ._11_15(rd));  // open: _0_25, _0_15
  or or_3 (or_3_out, addu, subu);
  CONTRIL contril_1 (
    .OP(splitter_1_op), .FUNCT(splitter_1_funct), .out_3(lw), .out_4(sw), .out_5(ori), .out_6(j),
    .out_7(beq), .out_8(jal), .out_9(lui), .out_10(addiu), .out_11(bne), .out_12(lb), .out_13(lh),
    .out_14(sb), .out_15(sh), .out_16(addu), .out_17(subu), .out_18(nop), .out_19(jr));
  or or_4 (or_4_out, addu, subu);
  buf or_5 (or_5_out, ori);  // OR_Gate
  buf or_6 (or_6_out, lw);  // OR_Gate
  Multiplexer #(.width(2), .enable("false")) multiplexer_1 (
    .in0(2'b00), .in1(2'b01), .out(multiplexer_1_out), .sel(or_2_out));
  Multiplexer #(.width(2), .enable("false")) multiplexer_2 (
    .in0(2'b00), .in1(2'b10), .out(multiplexer_2_out), .sel(or_3_out));
  Multiplexer #(.width(2), .enable("false")) multiplexer_3 (
    .in0(2'b00), .in1(2'b11), .out(multiplexer_3_out), .sel(jal));
  or or_7 (or_7_out, or_4_out, or_5_out);
  buf or_8 (or_8_out[0], lui);  // OR_Gate
  buf or_9 (or_8_out[1], jal);  // OR_Gate
  Multiplexer #(.width(2), .enable("false")) multiplexer_4 (
    .in0(2'b00), .in1(2'b10), .out(multiplexer_4_out), .sel(or_6_out));
  Multiplexer #(.width(2), .enable("false")) multiplexer_5 (
    .in0(2'b00), .in1(2'b01), .out(multiplexer_5_out), .sel(or_7_out));
  assign or_10_out = multiplexer_1_out | multiplexer_2_out | multiplexer_3_out;  // OR_Gate or_10, 2 bits wide
  Multiplexer #(.select(2), .width(32), .enable("false")) multiplexer_6 (
    .in0({32{1'b0}}), .in1(in_2), .in2(in_3), .out(out_8), .sel(or_8_out));  // open: in3
  Multiplexer #(.select(2), .width(5), .enable("false")) multiplexer_7 (
    .in0({5{1'b0}}), .in1(rt), .in2(rd), .in3({5{1'b1}}), .out(out_7), .sel(or_10_out));
  assign or_11_out = multiplexer_5_out | multiplexer_4_out;  // OR_Gate or_11, 2 bits wide
  Multiplexer #(.width(5), .enable("false")) multiplexer_8 (
    .in0({5{1'b0}}), .in1(splitter_1__21_25), .out(out_4), .sel(or_15_out));
  Multiplexer #(.width(5), .enable("false")) multiplexer_9 (.in0({5{1'b0}}), .in1(rt), .out(out_5), .sel(or_1_out));
  assign out_6 = {{2{1'b0}}, or_11_out};  // Bit_Extender bit_extender_1
  or or_12 (or_12_out, addu, subu);
  or or_13 (or_13_out, sw, lw);
  buf or_14 (or_14_out, ori);  // OR_Gate
  or or_15 (or_15_out, or_12_out, or_13_out, or_14_out);
endmodule

module M (
  input  [31:0] in_1,
  input  [31:0] alu,
  input  [31:0] alu_2,
  input  [31:0] pc_8,
  output [4:0] out_5,
  output [3:0] out_6,
  output [4:0] out_7,
  output [31:0] out_8
);

  wire addiu, addu, beq, bne, j, jal, jr, lb, lh, lui, lw, nop, nor_1_out, or_1_out, or_2_out, or_3_out,
       or_4_out, or_5_out, or_6_out, or_7_out, ori, sb, sh, subu, sw;
  wire [1:0] multiplexer_1_out, multiplexer_2_out, multiplexer_3_out, or_8_out, priority_encoder_1_out;
  wire [4:0] rd, rt;
  wire [5:0] splitter_1_funct, splitter_1_op;

  buf or_1 (or_1_out, sw);  // OR_Gate
  SPLITTER splitter_1 (
    .in_1(in_1), .OP(splitter_1_op), .FUNCT(splitter_1_funct), ._16_20(rt), ._11_15(rd));  // open: _0_25, _0_15, _21_25
  or or_2 (or_2_out, lw, ori, lui);
  CONTRIL contril_1 (
    .OP(splitter_1_op), .FUNCT(splitter_1_funct), .out_3(lw), .out_4(sw), .out_5(ori), .out_6(j),
    .out_7(beq), .out_8(jal), .out_9(lui), .out_10(addiu), .out_11(bne), .out_12(lb), .out_13(lh),
    .out_14(sb), .out_15(sh), .out_16(addu), .out_17(subu), .out_18(nop), .out_19(jr));
  or or_3 (or_3_out, addu, subu);
  or or_4 (or_4_out, addu, subu, ori);
  buf or_5 (or_5_out, lui);  // OR_Gate
  buf or_6 (or_6_out, jal);  // OR_Gate
  Priority_Encoder #(.select(2)) priority_encoder_1 (
    .in0(nor_1_out), .in1(or_4_out), .in2(or_5_out), .in3(or_6_out), .out(priority_encoder_1_out));  // open: gs, en_out, en_in
  buf or_7 (or_7_out, lw);  // OR_Gate
  Multiplexer #(.width(2), .enable("false")) multiplexer_1 (
    .in0(2'b00), .in1(2'b01), .out(multiplexer_1_out), .sel(or_2_out));
  Multiplexer #(.width(2), .enable("false")) multiplexer_2 (
    .in0(2'b00), .in1(2'b10), .out(multiplexer_2_out), .sel(or_3_out));
  Multiplexer #(.width(2), .enable("false")) multiplexer_3 (
    .in0(2'b00), .in1(2'b11), .out(multiplexer_3_out), .sel(jal));
  Multiplexer #(.select(2), .width(32), .enable("false")) multiplexer_4 (
    .in0({32{1'b0}}), .in1(alu), .in2(alu_2), .in3(pc_8), .out(out_8), .sel(priority_encoder_1_out));
  nor nor_1 (nor_1_out, or_4_out, or_5_out, or_6_out);
  assign out_6 = {{3{1'b0}}, or_7_out};  // Bit_Extender bit_extender_1
  Multiplexer #(.width(5), .enable("false")) multiplexer_5 (.in0({5{1'b0}}), .in1(rt), .out(out_5), .sel(or_1_out));
  Multiplexer #(.select(2), .width(5), .enable("false")) multiplexer_6 (
    .in0({5{1'b0}}), .in1(rt), .in2(rd), .in3({5{1'b1}}), .out(out_7), .sel(or_8_out));
  assign or_8_out = multiplexer_1_out | multiplexer_2_out | multiplexer_3_out;  // OR_Gate or_8, 2 bits wide
endmodule

module W (
  input  [31:0] in_1,
  input  [31:0] regdata,
  input  [31:0] alu,
  input  [31:0] ext,
  input  [31:0] pc_8,
  output [4:0] out_6,
  output [4:0] out_7,
  output [31:0] out_8
);

  wire addiu, addu, beq, bne, j, jal, jr, lb, lh, lui, lw, nop, nor_1_out, or_1_out, or_2_out, or_3_out,
       or_4_out, or_5_out, or_6_out, or_7_out, ori, sb, sh, subu, sw;
  wire [1:0] multiplexer_2_out, multiplexer_3_out, multiplexer_4_out, or_8_out, priority_encoder_1_out;
  wire [4:0] rd, rt;
  wire [5:0] splitter_1_funct, splitter_1_op;
  wire [31:0] multiplexer_1_out;

  buf or_1 (or_1_out, sw);  // OR_Gate
  SPLITTER splitter_1 (
    .in_1(in_1), .OP(splitter_1_op), .FUNCT(splitter_1_funct), ._16_20(rt), ._11_15(rd));  // open: _0_25, _0_15, _21_25
  or or_2 (or_2_out, lw, ori, lui);
  CONTRIL contril_1 (
    .OP(splitter_1_op), .FUNCT(splitter_1_funct), .out_3(lw), .out_4(sw), .out_5(ori), .out_6(j),
    .out_7(beq), .out_8(jal), .out_9(lui), .out_10(addiu), .out_11(bne), .out_12(lb), .out_13(lh),
    .out_14(sb), .out_15(sh), .out_16(addu), .out_17(subu), .out_18(nop), .out_19(jr));
  or or_3 (or_3_out, addu, subu);
  Multiplexer #(.width(32), .enable("false")) multiplexer_1 (
    .in0(regdata), .in1(alu), .out(multiplexer_1_out), .sel(or_4_out));
  or or_4 (or_4_out, addu, subu, ori);
  Multiplexer #(.width(2), .enable("false")) multiplexer_2 (
    .in0(2'b00), .in1(2'b01), .out(multiplexer_2_out), .sel(or_2_out));
  Multiplexer #(.width(2), .enable("false")) multiplexer_3 (
    .in0(2'b00), .in1(2'b10), .out(multiplexer_3_out), .sel(or_3_out));
  Multiplexer #(.width(2), .enable("false")) multiplexer_4 (
    .in0(2'b00), .in1(2'b11), .out(multiplexer_4_out), .sel(jal));
  or or_5 (or_5_out, addu, subu, ori);
  buf or_6 (or_6_out, lui);  // OR_Gate
  buf or_7 (or_7_out, jal);  // OR_Gate
  nor nor_1 (nor_1_out, or_5_out, or_6_out, or_7_out);
  Priority_Encoder #(.select(2)) priority_encoder_1 (
    .in0(nor_1_out), .in1(or_5_out), .in2(or_6_out), .in3(or_7_out), .out(priority_encoder_1_out));  // open: gs, en_out, en_in
  Multiplexer #(.select(2), .width(5), .enable("false")) multiplexer_5 (
    .in0({5{1'b0}}), .in1(rt), .in2(rd), .in3({5{1'b1}}), .out(out_7), .sel(or_8_out));
  assign or_8_out = multiplexer_2_out | multiplexer_3_out | multiplexer_4_out;  // OR_Gate or_8, 2 bits wide
  Multiplexer #(.select(2), .width(32), .enable("false")) multiplexer_6 (
    .in0({32{1'b0}}), .in1(multiplexer_1_out), .in2(ext), .in3(pc_8), .out(out_8),
    .sel(priority_encoder_1_out));
  Multiplexer #(.width(5), .enable("false")) multiplexer_7 (.in0({5{1'b0}}), .in1(rt), .out(out_6), .sel(or_1_out));
endmodule

module npcop (
  input  beq,
  input  jal,
  input  jal_2,
  input  jr,
  input  bne,
  output [2:0] out_6
);

  wire or_1_out;

  or or_1 (or_1_out, jal, jal_2);
  or or_2 (out_6[1], jr, or_1_out);
  or or_3 (out_6[0], jr, beq);

  assign out_6[2] = bne;
endmodule

module sblb (
  input  SB,
  input  LB,
  input  SH,
  input  LH,
  output [1:0] out_5
);

  buf or_1 (out_5[1], SH);  // OR_Gate
  buf or_2 (out_5[0], SB);  // OR_Gate
endmodule
